# Fritzing sketch touchswitch (saved by Fritzing 0.9.3b)
breadboards: 1

parts:
  TOUCH_SENSOR = TTP223B Capacitive Touch Sensor Module  # not connected
  Part1 = Arduino Uno (Rev3)
  LED1 = smd LED [color="Red (633nm)" package="0603 [SMD]"]
  R1 = Resistor [tolerance=±5% resistance=220 package="0805 [SMD]"]

nets:
  N1: Part1.D13/SCK, LED1.anode, R1.Pin_0, R1.Pin_1

custom parts:
  TTP223B Capacitive Touch Sensor Module: The TTP223B capacitive touch sensor module uses the TTP223B IC. The appropriate voltage is approximately 2 to 5.5 volts.
